# Fritzing sketch tree_stand (saved by Fritzing 0.9.10b)
breadboards: 1

parts:
  S2 = Pushbutton [package=THT]
  S4 = Pushbutton [package=THT]
  S1 = Pushbutton [package=THT]
  S3 = Pushbutton [package=THT]
  U1 = RJ45 Jack [package=rj45-8]

nets:
  N1: S2.leg0, S4.leg0, S1.leg0, S3.leg0, U1.2
  N2: S2.leg1, U1.6
  N3: S4.leg1, U1.8
  N4: S1.leg1, U1.5
  N5: S3.leg1, U1.7

custom parts:
  RJ45 Jack: RJ45 Jack Simple RJ45, 8-pin connection - connector for common Cat5, Cat5e, and Cat6 Ethernet cables. Footprint not yet proven in production. Connector sku is PRT-00643; Breakout PCB sku is BOB-00716.
