# Fritzing sketch tree_waterer (saved by Fritzing 0.9.10b)
breadboards: 1

parts:
  LED1 = LED - 5mm [color="Green (555nm)" current=0.030 package="5 mm [THT]"]
  LED2 = LED - 5mm [color="Green (555nm)" current=0.030 package="5 mm [THT]"]
  LED3 = LED - 5mm [color="Green (555nm)" current=0.030 package="5 mm [THT]"]
  LED4 = LED - 5mm [color="Green (555nm)" current=0.030 package="5 mm [THT]"]
  LED5 = LED - 5mm [color="Orange (620nm)" current=0.030 package="5 mm [THT]"]
  LED6 = LED - 5mm [color="Red (633nm)" current=0.030 package="5 mm [THT]"]
  LED7 = LED - 5mm [color="Blue (430nm)" current=0.030 package="5 mm [THT]"]
  LED8 = LED - 5mm [color="Blue (430nm)" current=0.030 package="5 mm [THT]"]
  R2 = Resistor [tolerance=±5% resistance=10k power=0.25 package=THT]
  Q1 = NPN-Transistor [part_number=PN2222A package="TO92 [THT]"]
  D1 = Rectifier Diode [part_number=1N4001 package="300 mil [THT]"]
  R3 = Resistor [tolerance=±5% resistance=220 power=0.25 package=THT]
  Pump = DC Motor [voltage_(max)=6V voltage_(min)=3V]
  Part1 = Arduino Uno (Rev3)
  R1 = Resistor [tolerance=±5% power=0.25 resistance=220 package=THT]
  J1 = screw terminal, 8 pins
  U1 = RJ45 Jack [package=rj45-8]

nets:
  N1: LED1.cathode, LED2.cathode, LED3.cathode, LED4.cathode, R1.Pin_1
  N2: LED1.anode, Part1.D3_PWM
  N3: LED2.anode, Part1.D4
  N4: LED3.anode, Part1.D5_PWM
  N5: LED4.anode, Part1.D6_PWM
  N6: LED5.cathode, LED6.cathode, LED7.cathode, LED8.cathode, R2.Pin_0
  N7: LED5.anode, Part1.D10_PWM/SS
  N8: LED6.anode, Part1.D9_PWM
  N9: LED7.anode, Part1.D7
  N10: LED8.anode, Part1.D8
  GND: R2.Pin_1, Q1.E, Part1.GND, R1.Pin_0, J1.pin5, J1.pin8, U1.2
  N11: Q1.B, R3.Pin_1
  N12: Q1.C, D1.anode, Pump.pin_1, J1.pin2
  VIN: D1.cathode, Pump.pin_2, Part1.VIN, J1.pin1
  D2: R3.Pin_0, Part1.D2
  A0: Part1.A0, U1.8
  A1: Part1.A1, U1.7
  A2: Part1.A2, U1.6
  A3: Part1.A3, U1.5
  A4: Part1.A4/SDA, J1.pin3
  A5: Part1.A5/SCL, J1.pin6
  5V: Part1.5V, J1.pin4, J1.pin7, U1.1

custom parts:
  RJ45 Jack: RJ45 Jack Simple RJ45, 8-pin connection - connector for common Cat5, Cat5e, and Cat6 Ethernet cables. Footprint not yet proven in production. Connector sku is PRT-00643; Breakout PCB sku is BOB-00716.
